# Fritzing sketch Flappy_duino (saved by Fritzing 0.8.5b)
breadboards: 1

parts:
  R1 = Rotary Potentiometer (Small) [maximum_resistance=100kΩ package=THT]
  S1 = Pushbutton [package="[THT]"]
  Componente1 = Arduino Uno (Rev3)
  R2 = Resistor [tolerance=±5% resistance=220 package=THT]

nets:
  N1: R1.leg1, S1.Pin_3, S1.Pin_4, Componente1.GND
  N2: R1.wiper, Componente1.A0
  N3: R1.leg2, Componente1.5V, R2.Pin_1
  N4: S1.Pin_1, S1.Pin_2, Componente1.D2, R2.Pin_0
